# Fritzing sketch GoPro Timelapse (saved by Fritzing 0.9.3b)
circuit board: 8.46667cm x 5.64444cm
breadboards: 1

parts:
  Part1 = Arduino Uno (Rev3)
  Part2 = Bluetooth HC-05 Macho
  LED1 = smd LED [color="Red (633nm)" package="0805 [SMD]"]
  J1 = Piezo Speaker
  LED2 = smd LED [color="Red (633nm)" package="0805 [SMD]"]
  J2 = Basic Servo
  R2 = Resistor [tolerance=±5% resistance=220 package=THT]
  R1 = Resistor [tolerance=±5% resistance=220 package=THT]

nets:
  N1: Part1.D10_PWM/SS, Part2.TXD
  N2: Part1.D11_PWM/MOSI, Part2.RXD
  N3: Part1.D12/MISO, R1.Pin_1
  N4: Part1.D13/SCK, R2.Pin_0
  GND: Part1.GND, Part2.GND, LED1.cathode, J1.pin1, LED2.cathode, J2.gnd
  N5: Part1.D3_PWM, J1.pin2
  N6: Part1.D5_PWM, J2.pulse
  VCC: Part1.5V, Part2.VCC, J2.vcc
  N7: LED1.anode, R1.Pin_0
  N8: LED2.anode, R2.Pin_1

// code stored in the sketch: Untitled2.ino

